// Logisim project adder.circ as structural Verilog: 3 circuits, main circuit main
module main (
  input  in_1,
  input  in_2,
  input  in_3,
  input  in_4,
  input  in_5,
  input  in_6,
  input  in_7,
  input  in_8,
  output out_9,
  output out_10,
  output out_11,
  output out_12
);

  wire full_adder_2_c, full_adder_3_c, half_adder_1_c;

  full_adder full_adder_1 (.B(in_1), .Cin(in_5), .in_3(full_adder_2_c), .S(out_9));  // open: C
  full_adder full_adder_2 (.B(in_2), .Cin(in_6), .in_3(full_adder_3_c), .C(full_adder_2_c), .S(out_10));
  full_adder full_adder_3 (.B(in_3), .Cin(in_7), .in_3(half_adder_1_c), .C(full_adder_3_c), .S(out_11));
  half_adder half_adder_1 (.A(in_4), .B(in_8), .S(out_12), .C(half_adder_1_c));

  // Notes on the sheet:
  //   Brian Chen
endmodule

module half_adder (
  input  A,
  input  B,
  output S,
  output C
);

  xor xor_1 (S, A, B);
  and and_1 (C, A, B);

  // Notes on the sheet:
  //   Half Adder
endmodule

module full_adder (
  input  B,
  input  Cin,
  input  in_3,
  output C,
  output S
);

  wire and_1_out, and_2_out, and_3_out, xor_1_out;

  and and_1 (and_1_out, B, Cin);
  and and_2 (and_2_out, B, in_3);
  and and_3 (and_3_out, Cin, in_3);
  xor xor_1 (xor_1_out, B, Cin);
  or or_1 (C, and_1_out, and_2_out, and_3_out);
  xor xor_2 (S, xor_1_out, in_3);

  // Notes on the sheet:
  //   A
endmodule
