// Logisim project lab04.circ as structural Verilog: 1 circuit, main circuit main
module main (
  input  in_1,
  input  in_2,
  output out_3
);

  wire and_1_out, and_2_out;

  and and_1 (and_1_out, in_1, in_2);
  buf and_2 (and_2_out, in_1);  // AND_Gate
  or or_1 (out_3, and_1_out, and_2_out);

  // Notes on the sheet:
  //   Brian Chen
endmodule
