// Logisim project question3.circ as structural Verilog: 1 circuit, main circuit main
module main (
  input  a,
  input  b,
  input  c,
  input  d,
  output out_5
);

  wire and_1_out, and_2_out, and_3_out, and_4_out, and_5_out, not_1_out, not_2_out, not_3_out, not_4_out,
       or_1_out;

  not not_1 (not_1_out, a);
  not not_2 (not_2_out, c);
  not not_3 (not_3_out, b);
  not not_4 (not_4_out, c);
  and and_1 (and_1_out, not_4_out, d);
  and and_2 (and_2_out, not_1_out, not_2_out);
  and and_3 (and_3_out, not_3_out, and_1_out);
  and and_4 (and_4_out, c, b);
  and and_5 (and_5_out, a, and_4_out);
  or or_1 (or_1_out, and_2_out, and_3_out);
  or or_2 (out_5, and_5_out, or_1_out);

  // Notes on the sheet:
  //   Brian Chen
endmodule
