// Logisim project question5.circ as structural Verilog: 1 circuit, main circuit main
module main (
  input  A,
  input  B,
  output out_3,
  output out_4,
  output out_5,
  output out_6
);

  wire not_1_out, not_2_out, not_3_out, not_4_out;

  not not_1 (not_1_out, A);
  not not_2 (not_2_out, B);
  not not_3 (not_3_out, A);
  not not_4 (not_4_out, B);
  and and_1 (out_3, not_1_out, not_2_out);
  and and_2 (out_4, not_3_out, B);
  and and_3 (out_5, A, not_4_out);
  and and_4 (out_6, A, B);
endmodule
