// Logisim project question1.circ as structural Verilog: 1 circuit, main circuit main
module main (
  input  in_1,
  input  in_2,
  input  in_3,
  output out_4,
  output out_5,
  output out_6,
  output out_7
);

  wire and_1_out, and_2_out, and_3_out, and_4_out, d_ff_2_q, not_1_out, not_2_out, not_3_out, not_4_out,
       not_5_out, not_6_out, or_1_out, or_2_out;

  not not_1 (not_1_out, out_4);
  and and_1 (and_1_out, not_1_out, not_2_out);
  not not_2 (not_2_out, d_ff_2_q);
  not not_3 (not_3_out, in_2);
  not not_4 (not_4_out, d_ff_2_q);
  and and_2 (and_2_out, not_4_out, not_5_out);
  not not_5 (not_5_out, in_3);
  and and_3 (and_3_out, and_1_out, not_3_out);
  and and_4 (and_4_out, out_4, and_2_out);
  or or_1 (or_1_out, out_4, d_ff_2_q);
  or or_2 (or_2_out, and_3_out, and_4_out);
  D_Flip_Flop d_ff_1 (.clk(in_1), .D(or_1_out), .Q(out_4));  // open: Qn, preset, reset
  D_Flip_Flop d_ff_2 (.clk(in_1), .D(or_2_out), .Q(d_ff_2_q));  // open: Qn, preset, reset
  not not_6 (not_6_out, out_4);
  and and_5 (out_5, not_6_out, d_ff_2_q);
  not not_7 (out_6, out_4);
  and and_6 (out_7, out_4, d_ff_2_q);

  // Notes on the sheet:
  //   Brian Chen
endmodule
