// Logisim project tinyproc5.circ as structural Verilog: 3 circuits, main circuit main
module main (
  input  Clock,
  output Range_is__8_to_7,
  output out_3,
  output [1:0] SR1,
  output [1:0] SR2,
  output [1:0] out_6,
  output [7:0] out_7,
  output [7:0] out_8,
  output out_9,
  output out_10,
  output out_11,
  output [7:0] DR_S1_S2_Op,
  output [1:0] Operation,
  output [7:0] out_14
);

  wire and_1_out, and_2_out, and_3_out, and_4_out, counter_1_p1, decoder_1_out0, decoder_1_out1,
       decoder_1_out2, decoder_1_out3;
  wire [7:0] adder_1_out, counter_1_p4, immediate_1_out_2, multiplier_1_out, ram_1_data, register_2_q,
       register_3_q, register_4_q, register_5_q, register_6_q, register_7_q, register_8_q, subtractor_1_out;

  controlunit controlunit_1 (
    .Get_Operands(out_11), .out_3(out_9), .Clk(Clock), .Compute(out_3), .Save_Registers(Range_is__8_to_7));
  // Counter counter_1: pin names not known; wires that end beside it: counter_1_p1, counter_1_p1, out_11, counter_1_p4
  Decoder #(.select(2), .enable("false")) decoder_1 (
    .out0(decoder_1_out0), .out1(decoder_1_out1), .out2(decoder_1_out2), .out3(decoder_1_out3),
    .sel(DR_S1_S2_Op[7:6]));
  and and_1 (and_1_out, Range_is__8_to_7, decoder_1_out0);
  and and_2 (and_2_out, Range_is__8_to_7, decoder_1_out1);
  and and_3 (and_3_out, Range_is__8_to_7, decoder_1_out2);
  and and_4 (and_4_out, Range_is__8_to_7, decoder_1_out3);
  RAM ram_1 (.addr(counter_1_p4), .data(ram_1_data));  // open: sel, clk, ld, clr
  Register register_1 (.D(ram_1_data), .Q(DR_S1_S2_Op), .clk(out_11));  // open: en, clr
  Register register_2 (.D(register_8_q), .Q(register_2_q), .clk(and_1_out));  // open: en, clr
  Multiplexer #(.select(2), .width(8), .enable("false")) multiplexer_1 (
    .in0(register_2_q), .in1(register_3_q), .in2(register_6_q), .in3(register_5_q), .out(out_7),
    .sel(DR_S1_S2_Op[5:4]));
  Adder adder_1 (.a(register_4_q), .b(register_7_q), .out(adder_1_out));  // open: cin, cout
  Register register_3 (.D(register_8_q), .Q(register_3_q), .clk(and_2_out));  // open: en, clr
  Register register_4 (.D(out_7), .Q(register_4_q), .clk(out_9));  // open: en, clr
  Subtractor subtractor_1 (.a(register_4_q), .b(register_7_q), .out(subtractor_1_out));  // open: bin, bout
  Multiplexer #(.select(2), .width(8), .enable("false")) multiplexer_2 (
    .in0(adder_1_out), .in1(subtractor_1_out), .in2(multiplier_1_out), .in3(immediate_1_out_2), .out(out_14),
    .sel(DR_S1_S2_Op[1:0]));
  Register register_5 (.D(register_8_q), .Q(register_5_q), .clk(and_4_out));  // open: en, clr
  Register register_6 (.D(register_8_q), .Q(register_6_q), .clk(and_3_out));  // open: en, clr
  Multiplexer #(.select(2), .width(8), .enable("false")) multiplexer_3 (
    .in0(register_2_q), .in1(register_3_q), .in2(register_6_q), .in3(register_5_q), .out(out_8),
    .sel(DR_S1_S2_Op[3:2]));
  Multiplier multiplier_1 (.a(register_4_q), .b(register_7_q), .out(multiplier_1_out));  // open: cin, cout
  Register register_7 (.D(out_8), .Q(register_7_q), .clk(out_9));  // open: en, clr
  immediate immediate_1 (.in_1(DR_S1_S2_Op), .out_2(immediate_1_out_2));
  Register register_8 (.D(out_14), .Q(register_8_q), .clk(out_3));  // open: en, clr

  assign Operation = DR_S1_S2_Op[1:0];
  assign out_6 = DR_S1_S2_Op[7:6];
  assign out_10 = out_9;
  assign SR1 = DR_S1_S2_Op[5:4];
  assign SR2 = DR_S1_S2_Op[3:2];

  // Other names for the same wires on the sheet: EX = out_3; O = out_9; STORE = Range_is__8_to_7

  // Notes on the sheet:
  //   Instructions:
  //   R3 = 2
  //   R2 = 3
  //   R1 = 1
  //   instruction)
  //   Format: DR SR1 SR2 Op
  //   Opcodes: 00 Add
  //   Opcodes: 01 Sub
  //   Opcodes: 10 Mul
  //   Opcodes: 11 load imm.
  //   Simple Program:
  //   11 0010 11 = CB
  //   10 0011 11 = 8F
  //   R0 = R2 * R3
  //   00 10 11 10 = 2E
  //   01 0001 11 = 47
  //   R2 = R0 - R1
  //   10 00 01 01 = 85
  //   R0 = R0 + R0
  //   00 00 00 00 = 00
  //   (this doubles R0
  //   for each "blank"
  //   Machine Code
  //   CB 8F 2E 47 85
  //   Destination Reg DR
  //   Program
  //   Counter
  //   Fetch Instruction
  //   For load immediate, the
  //   value is taken from the middle
  //   4 bits (sign extended)
  //   Save Register/Write
  //   Main Memory
  //   Inst. Reg
  //   TinyProc 5 - A Tiny (almost) Microprocessor
  //   Four registers, four op codes, simple fetch/store control unit
  //   Current Instruction
  //   R0,00
  //   REGISTERS
  //   R1,01
  //   R2,10
  //   For load immediate, the middle 4 bits are routed to the dest. register
  //   R3,11
  //   Sign Extend
  //   Arithmetic/Logic Unit (ALU)
endmodule

module immediate (
  input  [7:0] in_1,
  output [7:0] out_2
);


  assign out_2 = {{5{in_1[5]}}, in_1[4:2]};
endmodule

module controlunit (
  input  Clk,
  output Get_Operands,
  output out_3,
  output Compute,
  output Save_Registers
);

  wire [1:0] counter_1_q;

  Decoder #(.select(2), .enable("false")) decoder_1 (
    .out0(Get_Operands), .out1(out_3), .out2(Compute), .out3(Save_Registers), .sel(counter_1_q));
  Counter #(.width(2), .max('h3)) counter_1 (
    .D(counter_1_q), .Q(counter_1_q), .clk(Clk));  // open: load, count, carry, clr

  // Notes on the sheet:
  //   Fetch Instruction
endmodule
